# Fritzing sketch thermostat (saved by Fritzing 0.9.3b)
breadboards: 2

parts:
  Part1 = Adafruit Feather M0 WINC1500 [part_number="Adafruit #3010"]
  RHT1 = Humidity and Temperature Sensor RHT03
  C1 = Electrolytic Capacitor [capacitance=10µF voltage=50V package="100 mil [THT, electrolytic]"]
  C2 = Electrolytic Capacitor [capacitance=10µF voltage=10V package="100 mil [THT, electrolytic]"]
  Pins_1-15_LtoR = screw terminal, 15 pins
  5Vout_24Vin = screw terminal, 4 pins
  R7 = Resistor [tolerance=±5% resistance=10k package=THT]
  R8 = Resistor [tolerance=±5% resistance=10k package=THT]
  R9 = Resistor [tolerance=±5% resistance=10k package=THT]
  R10 = Resistor [tolerance=±5% resistance=1k package=THT]
  R11 = Resistor [tolerance=±5% resistance=1k package=THT]
  R12 = Resistor [tolerance=±5% resistance=10k package=THT]
  CUI_P1 = DC-DC Regulator [part_number=P7805-Q24-S5-5]
  uSD_Board1 = Level Shifting uSD Breakout
  S1 = Momentary Switch [package=ksa_sealed_tac_switch]
  S2 = Momentary Switch [package=ksa_sealed_tac_switch]
  S3 = Momentary Switch [package=ksa_sealed_tac_switch]

nets:
  N1: Part1.MISO, uSD_Board1.DO
  N2: Part1.MOSI, uSD_Board1.DI
  N3: Part1.SCK, uSD_Board1.SCK
  N4: Part1.A5, Part1.!RESET
  N5: Part1.A4, S1.4
  N6: Part1.A3, Pins_1-15_LtoR.pin14
  N7: Part1.A2, Pins_1-15_LtoR.pin13
  N8: Part1.A1, Pins_1-15_LtoR.pin10
  N9: Part1.A0, Pins_1-15_LtoR.pin9
  GND: Part1.GND, RHT1.GND_1, Pins_1-15_LtoR.pin2, Pins_1-15_LtoR.pin5, Pins_1-15_LtoR.pin8, Pins_1-15_LtoR.pin12, R7.Pin_1, R8.Pin_1, R9.Pin_1, uSD_Board1.GND
  VCC: Part1.+3V3, RHT1.Vcc, Pins_1-15_LtoR.pin4, R12.Pin_0, uSD_Board1.VCC, S1.1, S2.1, S3.1
  N10: Part1.VBUS, Pins_1-15_LtoR.pin11, Pins_1-15_LtoR.pin15
  N11: Part1.D13, R10.Pin_0
  N12: Part1.D12, R11.Pin_0
  N13: Part1.D11, S2.4
  N14: Part1.D10, uSD_Board1.CS
  N15: Part1.D6, S3.4
  N16: Part1.D5, RHT1.Data-signal, R12.Pin_1
  N17: Part1.SCL, Pins_1-15_LtoR.pin7
  N18: Part1.SDA, Pins_1-15_LtoR.pin6
  N19: C1.-, C2.-, 5Vout_24Vin.pin1, 5Vout_24Vin.pin3, CUI_P1.Ground
  N20: C1.+, 5Vout_24Vin.pin2, CUI_P1.Vin
  N21: C2.+, 5Vout_24Vin.pin4, CUI_P1.Vout
  N22: Pins_1-15_LtoR.pin1, R10.Pin_1
  N23: Pins_1-15_LtoR.pin3, R11.Pin_1
  N24: R7.Pin_0, S1.3
  N25: R8.Pin_0, S3.3
  N26: R9.Pin_0, S2.3

notes:
  1-3: RGB LED
  1: Red
  2: Ground
  3: Green
  4-7: OLED Display
  4: 3.3V
  5: Ground
  6: SDA
  7: SCL
  8-11: Relays 1&2
  8: Ground
  9: Relay 1 (fan)
  10: Relay 2 (compressor)
  11: 5V
  12-15: Relays 3&4
  12: Ground
  13: Relay 3 (reversing valve)
  14: Relay 4 (aux heat)
  15: 5V

custom parts:
  Adafruit Feather M0 WINC1500: This is the Adafruit Feather M0 WiFi w/ATWINC1500 - our take on an 'all-in-one' Arduino-compatible + high speed, reliable WiFi with built in USB and battery charging. Its an Adafruit Feather M0 with a WiFi module, ready to rock! Connect your Feather to the Internet with this fine new FCC-certified WiFi module from Atmel. This 802.11bgn-capable WiFi module is the best new thing for networking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
  DC-DC Regulator: DC-DC Switching Regulator CUI P/N: P7805-Q24-S5-5 6.5-32V input (24V nom) 5V output 500mA max output
  Level Shifting uSD Breakout: Breakout board for the TI TXB0104 bi-directional level shifter IC. VccA should be lower than VccB. VccA can range from 1.2V to 3.6V, and VCCB can range from 1.65V to 5.5V.
